# Fritzing sketch schematic_small (saved by Fritzing 0.9.3b)
breadboards: 1

parts:
  DFRobot_DFPlayer_Mini1 = DFRobot DFPlayer Mini [part_number=DFR0299]
  SP1 = SPEAKER [package=pcb_mount_speaker]
  S1 = Round Pushbutton
  S2 = Round Pushbutton
  S9 = Round Pushbutton
  VCC1 = Battery
  LED1 = smd LED [color="Red (633nm)" package="1206 [SMD]"]

nets:
  N1: DFRobot_DFPlayer_Mini1.VCC, VCC1.+
  N2: DFRobot_DFPlayer_Mini1.SPK_1, SP1.-
  N3: DFRobot_DFPlayer_Mini1.GND-1, DFRobot_DFPlayer_Mini1.GND-2, S1.leg0, S2.leg0, S9.leg0, LED1.cathode
  N4: DFRobot_DFPlayer_Mini1.SPK_2, SP1.+
  N5: DFRobot_DFPlayer_Mini1.IO_1, S2.leg1
  N6: DFRobot_DFPlayer_Mini1.IO_2, S9.leg1
  N7: S1.leg1, VCC1.-
